// Logisim project nbit_arithmetic_unit_logisim.circ as structural Verilog: 10 circuits, main circuit B_input_logic
module B_input_logic (
  input  B,
  input  S0,
  input  S1,
  output Y
);

  wire and_1_out, and_2_out, not_1_out;

  not not_1 (not_1_out, B);
  and and_1 (and_1_out, B, S0);
  and and_2 (and_2_out, S1, not_1_out);
  or or_1 (Y, and_1_out, and_2_out);
endmodule

module Half_adder (
  input  InputA,
  input  InputB,
  output Sum,
  output Carry
);

  xor xor_1 (Sum, InputA, InputB);
  and and_1 (Carry, InputA, InputB);
endmodule

module Full_adder (
  input  InputC,
  input  InputA,
  input  InputB,
  output Sum,
  output Carry
);

  wire half_adder_1_carry, half_adder_1_sum, half_adder_2_carry;

  Half_adder half_adder_1 (.InputA(InputA), .InputB(InputB), .Sum(half_adder_1_sum), .Carry(half_adder_1_carry));
  Half_adder half_adder_2 (.InputA(InputC), .InputB(half_adder_1_sum), .Sum(Sum), .Carry(half_adder_2_carry));
  or or_1 (Carry, half_adder_2_carry, half_adder_1_carry);
endmodule

module B_input_logic_Nbit (
  input  B0,
  input  S0,
  input  S1,
  input  B1,
  input  B2,
  input  B3,
  output Y0,
  output Y1,
  output Y2,
  output Y3
);

  B_input_logic b_input_logic_1 (.B(B0), .S0(S0), .S1(S1), .Y(Y0));
  B_input_logic b_input_logic_2 (.B(B1), .S0(S0), .S1(S1), .Y(Y1));
  B_input_logic b_input_logic_3 (.B(B2), .S0(S0), .S1(S1), .Y(Y2));
  B_input_logic b_input_logic_4 (.B(B3), .S0(S0), .S1(S1), .Y(Y3));
endmodule

module Nbit_arithmetic_unit (
  input  Cin,
  input  A0,
  input  A1,
  input  B0,
  input  S0,
  input  S1,
  input  B1,
  input  B2,
  input  B3,
  input  A2,
  input  A3,
  output G0,
  output G1,
  output G2,
  output G3,
  output Cout
);

  wire b_input_logic_nbit_1_y0, b_input_logic_nbit_1_y1, b_input_logic_nbit_1_y2, b_input_logic_nbit_1_y3,
       full_adder_1_carry, full_adder_2_carry, full_adder_3_carry;

  B_input_logic_Nbit b_input_logic_nbit_1 (
    .B0(B0), .S0(S0), .S1(S1), .B1(B1), .B2(B2), .B3(B3), .Y0(b_input_logic_nbit_1_y0),
    .Y1(b_input_logic_nbit_1_y1), .Y2(b_input_logic_nbit_1_y2), .Y3(b_input_logic_nbit_1_y3));
  Full_adder full_adder_1 (
    .InputC(Cin), .InputA(A0), .InputB(b_input_logic_nbit_1_y0), .Sum(G0), .Carry(full_adder_1_carry));
  Full_adder full_adder_2 (
    .InputC(full_adder_1_carry), .InputA(A1), .InputB(b_input_logic_nbit_1_y1), .Sum(G1),
    .Carry(full_adder_2_carry));
  Full_adder full_adder_3 (
    .InputC(full_adder_2_carry), .InputA(A2), .InputB(b_input_logic_nbit_1_y2), .Sum(G2),
    .Carry(full_adder_3_carry));
  // Full_adder full_adder_4: pin names not known; wires that end beside it: full_adder_3_carry, b_input_logic_nbit_1_y3, A3, G3, Cout
endmodule

module OneBit_arithmetic_unit (
  input  Cin,
  input  A,
  input  B,
  input  S0,
  input  S1,
  output G,
  output Cout
);

  wire b_input_logic_1_y;

  B_input_logic b_input_logic_1 (.B(B), .S0(S0), .S1(S1), .Y(b_input_logic_1_y));
  Full_adder full_adder_1 (.InputC(Cin), .InputA(A), .InputB(b_input_logic_1_y), .Sum(G), .Carry(Cout));
endmodule

module binputtest (
  output Y
);

  wire and_1_out, and_2_out, B_out, not_1_out, S0_out, S1_out;

  Clock B (.out(B_out));
  Clock #(.highDuration(2), .lowDuration(2)) S0 (.out(S0_out));
  Clock #(.highDuration(4), .lowDuration(4)) S1 (.out(S1_out));
  not not_1 (not_1_out, B_out);
  and and_1 (and_1_out, B_out, S0_out);
  and and_2 (and_2_out, S1_out, not_1_out);
  or or_1 (Y, and_1_out, and_2_out);
endmodule

module binputnbittest (
  output Y0,
  output Y1,
  output Y2,
  output Y3
);

  wire B0_out, B1_out, B2_out, B3_out, S0_out, S1_out;

  Clock S0 (.out(S0_out));
  Clock #(.highDuration(2), .lowDuration(2)) S1 (.out(S1_out));
  Clock #(.highDuration(4), .lowDuration(4)) B0 (.out(B0_out));
  Clock #(.highDuration(8), .lowDuration(8)) B1 (.out(B1_out));
  Clock #(.highDuration(16), .lowDuration(16)) B2 (.out(B2_out));
  Clock #(.highDuration(32), .lowDuration(32)) B3 (.out(B3_out));
  B_input_logic b_input_logic_1 (.B(B0_out), .S0(S0_out), .S1(S1_out), .Y(Y0));
  B_input_logic b_input_logic_2 (.B(B1_out), .S0(S0_out), .S1(S1_out), .Y(Y1));
  B_input_logic b_input_logic_3 (.B(B2_out), .S0(S0_out), .S1(S1_out), .Y(Y2));
  B_input_logic b_input_logic_4 (.B(B3_out), .S0(S0_out), .S1(S1_out), .Y(Y3));
endmodule

module arithmeticunit1bittest (
  output G,
  output Cout
);

  wire A_out, b_input_logic_1_y, B_out, Cin_out, S0_out, S1_out;

  Clock Cin (.out(Cin_out));
  Clock #(.highDuration(2), .lowDuration(2)) A (.out(A_out));
  Clock #(.highDuration(4), .lowDuration(4)) B (.out(B_out));
  Clock #(.highDuration(8), .lowDuration(8)) S0 (.out(S0_out));
  Clock #(.highDuration(16), .lowDuration(16)) S1 (.out(S1_out));
  B_input_logic b_input_logic_1 (.B(B_out), .S0(S0_out), .S1(S1_out), .Y(b_input_logic_1_y));
  Full_adder full_adder_1 (.InputC(Cin_out), .InputA(A_out), .InputB(b_input_logic_1_y), .Sum(G), .Carry(Cout));
endmodule

module arithmeticunitnbittest (
  output G0,
  output G1,
  output G2,
  output G3,
  output Cout
);

  wire A0_out, A1_out, A2_out, A3_out, B0_out, B1_out, B2_out, B3_out, b_input_logic_nbit_1_y0,
       b_input_logic_nbit_1_y1, b_input_logic_nbit_1_y2, b_input_logic_nbit_1_y3, Cin_out,
       full_adder_1_carry, full_adder_2_carry, full_adder_3_carry, S0_out, S1_out;

  Clock B0 (.out(B0_out));
  Clock #(.highDuration(16), .lowDuration(16)) S0 (.out(S0_out));
  Clock #(.highDuration(32), .lowDuration(32)) S1 (.out(S1_out));
  Clock #(.highDuration(2), .lowDuration(2)) B1 (.out(B1_out));
  Clock #(.highDuration(4), .lowDuration(4)) B2 (.out(B2_out));
  Clock #(.highDuration(8), .lowDuration(8)) B3 (.out(B3_out));
  B_input_logic_Nbit b_input_logic_nbit_1 (
    .B0(B0_out), .S0(S0_out), .S1(S1_out), .B1(B1_out), .B2(B2_out), .B3(B3_out),
    .Y0(b_input_logic_nbit_1_y0), .Y1(b_input_logic_nbit_1_y1), .Y2(b_input_logic_nbit_1_y2),
    .Y3(b_input_logic_nbit_1_y3));
  Clock #(.highDuration(64), .lowDuration(64)) Cin (.out(Cin_out));
  Clock #(.highDuration(128), .lowDuration(128)) A0 (.out(A0_out));
  Clock #(.highDuration(256), .lowDuration(256)) A1 (.out(A1_out));
  Clock #(.highDuration(512), .lowDuration(512)) A2 (.out(A2_out));
  Clock #(.highDuration(1024), .lowDuration(1024)) A3 (.out(A3_out));
  Full_adder full_adder_1 (
    .InputC(Cin_out), .InputA(A0_out), .InputB(b_input_logic_nbit_1_y0), .Sum(G0), .Carry(full_adder_1_carry));
  Full_adder full_adder_2 (
    .InputC(full_adder_1_carry), .InputA(A1_out), .InputB(b_input_logic_nbit_1_y1), .Sum(G1),
    .Carry(full_adder_2_carry));
  Full_adder full_adder_3 (
    .InputC(full_adder_2_carry), .InputA(A2_out), .InputB(b_input_logic_nbit_1_y2), .Sum(G2),
    .Carry(full_adder_3_carry));
  Full_adder full_adder_4 (
    .InputC(full_adder_3_carry), .InputA(A3_out), .InputB(b_input_logic_nbit_1_y3), .Sum(G3), .Carry(Cout));
endmodule
